// Logisim project 4bit_simple_xor_cypher.circ as structural Verilog: 1 circuit, main circuit main
module main (
  input  I1,
  input  I2,
  input  I3,
  input  I4
);

  wire button_1_out, CLK, d_ff_4_q, ENCRYPT_I1, ENCRYPT_I2, ENCRYPT_I3, ENCRYPT_I4, K1, K2, K3, K4,
       xor_6_out, xor_7_out, xor_8_out, xor_9_out;

  Clock clock_1 (.out(CLK));
  D_Flip_Flop d_ff_1 (.clk(CLK), .D(K4), .Q(K1), .preset(button_1_out));  // open: Qn, en, reset
  Button button_1 (.out(button_1_out));
  D_Flip_Flop d_ff_2 (.clk(CLK), .D(K1), .Q(K2));  // open: Qn, preset, en, reset
  xor xor_1 (ENCRYPT_I1, I1, K1);
  LED led_1 (.in(ENCRYPT_I1));
  LED led_2 (.in(ENCRYPT_I2));
  xor xor_2 (ENCRYPT_I2, I2, K2);
  LED led_3 (.in(ENCRYPT_I3));
  xor xor_3 (ENCRYPT_I3, I3, K3);
  xor xor_4 (ENCRYPT_I4, I4, K4);
  LED led_4 (.in(ENCRYPT_I4));
  D_Flip_Flop d_ff_3 (.clk(CLK), .D(K2), .Q(K3));  // open: Qn, preset, en, reset
  D_Flip_Flop d_ff_4 (.clk(CLK), .D(K3), .Q(d_ff_4_q));  // open: Qn, preset, en, reset
  xor xor_5 (K4, d_ff_4_q, K3);
  xor xor_6 (xor_6_out, ENCRYPT_I1, K1);
  xor xor_7 (xor_7_out, ENCRYPT_I2, K2);
  xor xor_8 (xor_8_out, ENCRYPT_I3, K3);
  xor xor_9 (xor_9_out, ENCRYPT_I4, K4);
  LED led_5 (.in(xor_6_out));
  LED led_6 (.in(xor_7_out));
  LED led_7 (.in(xor_8_out));
  LED led_8 (.in(xor_9_out));
endmodule
