// Logisim project complex_keygen_text_cipher.circ as structural Verilog: 2 circuits, main circuit main
module main (
);

  wire button_1_out, CLK, clock_1_out, d_ff_7_q, ENCRYPTED_I1, ENCRYPTED_I2, ENCRYPTED_I3, ENCRYPTED_I4,
       ENCRYPTED_I5, ENCRYPTED_I6, ENCRYPTED_I7, FF1, FF2, FF3, FF4, FF5, FF6, FF7, I1, I2, I3, I4, I5, I6,
       I7, K1, K2, K3, K4, K5, K6, K7, KB_BUFFER, not_1_out, not_2_out, not_3_out, not_4_out, not_5_out,
       not_6_out, not_7_out, not_8_out, not_9_out, not_10_out, not_11_out, not_12_out, not_13_out,
       not_14_out, not_15_out, xor_15_out;
  wire [6:0] xor_8_out;

  not not_1 (not_1_out, CLK);
  Keyboard keyboard_1 (.clk(not_1_out), .avail(KB_BUFFER), .data({I7, I6, I5, I4, I3, I2, I1}));  // open: re, clr
  Clock clock_1 (.out(clock_1_out));
  and and_1 (CLK, clock_1_out, KB_BUFFER);
  Button button_1 (.out(button_1_out));
  D_Flip_Flop d_ff_1 (.clk(CLK), .D(FF7), .Q(FF1), .preset(button_1_out));  // open: Qn, en, reset
  Mixer mixer_1 (.in_1(FF4), .in_2(FF3), .in_3(FF1), .out_4(K1));
  not not_2 (not_2_out, K4);
  not not_3 (not_3_out, K2);
  not not_4 (not_4_out, K5);
  not not_5 (not_5_out, K1);
  not not_6 (not_6_out, K7);
  not not_7 (not_7_out, K3);
  not not_8 (not_8_out, K6);
  D_Flip_Flop d_ff_2 (.clk(CLK), .D(FF1), .Q(FF2));  // open: Qn, preset, en, reset
  Mixer mixer_2 (.in_1(FF6), .in_2(FF3), .in_3(FF2), .out_4(K2));
  xor xor_1 (ENCRYPTED_I1, I1, not_2_out);
  xor xor_2 (ENCRYPTED_I2, I2, not_3_out);
  xor xor_3 (ENCRYPTED_I3, I3, not_4_out);
  xor xor_4 (ENCRYPTED_I4, I4, not_5_out);
  xor xor_5 (ENCRYPTED_I5, I5, not_6_out);
  xor xor_6 (ENCRYPTED_I6, I6, not_7_out);
  xor xor_7 (ENCRYPTED_I7, I7, not_8_out);
  D_Flip_Flop d_ff_3 (.clk(CLK), .D(FF2), .Q(FF3));  // open: Qn, preset, en, reset
  Mixer mixer_3 (.in_1(FF5), .in_2(FF1), .in_3(FF7), .out_4(K3));
  Mixer mixer_4 (.in_1(FF5), .in_2(FF7), .in_3(FF6), .out_4(K4));
  D_Flip_Flop d_ff_4 (.clk(CLK), .D(FF3), .Q(FF4));  // open: Qn, preset, en, reset
  xor xor_8 (xor_8_out[0], ENCRYPTED_I1, not_9_out);
  not not_9 (not_9_out, K4);
  xor xor_9 (xor_8_out[1], ENCRYPTED_I2, not_10_out);
  not not_10 (not_10_out, K2);
  xor xor_10 (xor_8_out[2], ENCRYPTED_I3, not_11_out);
  not not_11 (not_11_out, K5);
  xor xor_11 (xor_8_out[3], ENCRYPTED_I4, not_12_out);
  not not_12 (not_12_out, K1);
  xor xor_12 (xor_8_out[4], ENCRYPTED_I5, not_13_out);
  not not_13 (not_13_out, K7);
  xor xor_13 (xor_8_out[5], ENCRYPTED_I6, not_14_out);
  not not_14 (not_14_out, K3);
  xor xor_14 (xor_8_out[6], ENCRYPTED_I7, not_15_out);
  not not_15 (not_15_out, K6);
  D_Flip_Flop d_ff_5 (.clk(CLK), .D(FF4), .Q(FF5));  // open: Qn, preset, en, reset
  Mixer mixer_5 (.in_1(FF4), .in_2(FF1), .in_3(FF2), .out_4(K5));
  D_Flip_Flop d_ff_6 (.clk(CLK), .D(FF5), .Q(FF6));  // open: Qn, preset, en, reset
  Mixer mixer_6 (.in_1(FF6), .in_2(FF2), .in_3(FF3), .out_4(K6));
  D_Flip_Flop d_ff_7 (.clk(CLK), .D(FF6), .Q(d_ff_7_q));  // open: Qn, preset, en, reset
  Mixer mixer_7 (.in_1(FF4), .in_2(FF7), .in_3(FF3), .out_4(K7));
  TTY tty_1 (.data(xor_8_out), .clk(CLK));  // open: we, clr
  xor xor_15 (xor_15_out, d_ff_7_q, FF6);
  not not_16 (FF7, xor_15_out);
  Hex_Digit_Display hex_digit_display_1 (.value({ENCRYPTED_I4, ENCRYPTED_I3, ENCRYPTED_I2, ENCRYPTED_I1}));  // open: dp
  Hex_Digit_Display hex_digit_display_2 (.value({1'b0, ENCRYPTED_I7, ENCRYPTED_I6, ENCRYPTED_I5}));  // open: dp
endmodule

module Mixer (
  input  in_1,
  input  in_2,
  input  in_3,
  output out_4
);

  wire and_1_out;

  and and_1 (and_1_out, in_1, in_2);
  xor xor_1 (out_4, and_1_out, in_3);
endmodule
