// Logisim project complex_text_cipher.circ as structural Verilog: 3 circuits, main circuit main
module main (
);

  wire button_1_out, CLK, clock_1_out, d_ff_7_q, ENCRYPTED_I1, ENCRYPTED_I2, ENCRYPTED_I3, ENCRYPTED_I4,
       ENCRYPTED_I5, ENCRYPTED_I6, ENCRYPTED_I7, FF1, FF2, FF3, FF4, FF5, FF6, FF7, I1, I2, I3, I4, K1, K2,
       K3, K4, K5, K6, K7, KB_BUFFER, not_1_out, not_2_out, not_3_out, not_4_out, not_5_out, not_6_out,
       not_7_out, not_8_out, not_9_out, not_10_out, not_11_out, not_12_out, not_13_out, not_14_out,
       not_15_out, not_16_out, not_17_out, xor_17_out;
  wire [2:0] ANCHOR, ANCHOR2;
  wire [3:0] FeistelMixer_1_out_3, FeistelMixer_2_out_3, TARGET, TARGET2, xor_16_out;

  Keyboard keyboard_1 (.clk(not_1_out), .avail(KB_BUFFER), .data({ANCHOR, TARGET}));  // open: re, clr
  not not_1 (not_1_out, CLK);
  Complex_Encrypter FeistelMixer_1 (.in_1(ANCHOR), .in_2({K6, K2, K4, K1}), .out_3(FeistelMixer_1_out_3));
  assign {I4, I3, I2, I1} = FeistelMixer_1_out_3 ^ TARGET;  // XOR_Gate xor_1, 4 bits wide
  Clock clock_1 (.out(clock_1_out));
  and and_1 (CLK, clock_1_out, KB_BUFFER);
  not not_2 (not_2_out, K4);
  not not_3 (not_3_out, K2);
  not not_4 (not_4_out, K5);
  not not_5 (not_5_out, K1);
  not not_6 (not_6_out, K7);
  not not_7 (not_7_out, K3);
  not not_8 (not_8_out, K6);
  Button button_1 (.out(button_1_out));
  xor xor_2 (ENCRYPTED_I1, I1, not_2_out);
  xor xor_3 (ENCRYPTED_I2, I2, not_3_out);
  xor xor_4 (ENCRYPTED_I3, I3, not_4_out);
  xor xor_5 (ENCRYPTED_I4, I4, not_5_out);
  xor xor_6 (ENCRYPTED_I5, ANCHOR[0], not_6_out);
  xor xor_7 (ENCRYPTED_I6, ANCHOR[1], not_7_out);
  xor xor_8 (ENCRYPTED_I7, ANCHOR[2], not_8_out);
  D_Flip_Flop d_ff_1 (.clk(CLK), .D(FF7), .Q(FF1), .preset(button_1_out));  // open: Qn, en, reset
  KeyGenMixer Keymixer_1 (.in_1(FF4), .in_2(FF3), .in_3(FF1), .out_4(K1));
  D_Flip_Flop d_ff_2 (.clk(CLK), .D(FF1), .Q(FF2));  // open: Qn, preset, en, reset
  KeyGenMixer Keymixer_2 (.in_1(FF6), .in_2(FF3), .in_3(FF2), .out_4(K2));
  D_Flip_Flop d_ff_3 (.clk(CLK), .D(FF2), .Q(FF3));  // open: Qn, preset, en, reset
  KeyGenMixer Keymixer_3 (.in_1(FF5), .in_2(FF1), .in_3(FF7), .out_4(K3));
  xor xor_9 (TARGET2[0], ENCRYPTED_I1, not_9_out);
  not not_9 (not_9_out, K4);
  xor xor_10 (TARGET2[1], ENCRYPTED_I2, not_10_out);
  not not_10 (not_10_out, K2);
  xor xor_11 (TARGET2[2], ENCRYPTED_I3, not_11_out);
  not not_11 (not_11_out, K5);
  xor xor_12 (TARGET2[3], ENCRYPTED_I4, not_12_out);
  not not_12 (not_12_out, K1);
  xor xor_13 (ANCHOR2[0], ENCRYPTED_I5, not_13_out);
  not not_13 (not_13_out, K7);
  xor xor_14 (ANCHOR2[1], ENCRYPTED_I6, not_14_out);
  not not_14 (not_14_out, K3);
  xor xor_15 (ANCHOR2[2], ENCRYPTED_I7, not_15_out);
  not not_15 (not_15_out, K6);
  KeyGenMixer Keymixer_4 (.in_1(FF5), .in_2(FF7), .in_3(FF6), .out_4(K4));
  D_Flip_Flop d_ff_4 (.clk(CLK), .D(FF3), .Q(FF4));  // open: Qn, preset, en, reset
  D_Flip_Flop d_ff_5 (.clk(CLK), .D(FF4), .Q(FF5));  // open: Qn, preset, en, reset
  KeyGenMixer Keymixer_5 (.in_1(FF4), .in_2(FF1), .in_3(FF2), .out_4(K5));
  Complex_Encrypter FeistelMixer_2 (.in_1(ANCHOR2), .in_2({K6, K2, K4, K1}), .out_3(FeistelMixer_2_out_3));
  D_Flip_Flop d_ff_6 (.clk(CLK), .D(FF5), .Q(FF6));  // open: Qn, preset, en, reset
  KeyGenMixer Keymixer_6 (.in_1(FF6), .in_2(FF2), .in_3(FF3), .out_4(K6));
  assign xor_16_out = FeistelMixer_2_out_3 ^ TARGET2;  // XOR_Gate xor_16, 4 bits wide
  not not_16 (not_16_out, CLK);
  TTY tty_1 (
    .data({ENCRYPTED_I7, ENCRYPTED_I6, ENCRYPTED_I5, ENCRYPTED_I4, ENCRYPTED_I3, ENCRYPTED_I2, ENCRYPTED_I1}),
    .clk(not_16_out));  // open: we, clr
  D_Flip_Flop d_ff_7 (.clk(CLK), .D(FF6), .Q(d_ff_7_q));  // open: Qn, preset, en, reset
  KeyGenMixer Keymixer_7 (.in_1(FF4), .in_2(FF7), .in_3(FF3), .out_4(K7));
  TTY tty_2 (.data({ANCHOR2, xor_16_out}), .clk(not_17_out));  // open: we, clr
  not not_17 (not_17_out, CLK);
  Hex_Digit_Display hex_digit_display_1 (.value({ENCRYPTED_I4, ENCRYPTED_I3, ENCRYPTED_I2, ENCRYPTED_I1}));  // open: dp
  xor xor_17 (xor_17_out, d_ff_7_q, FF6);
  Hex_Digit_Display hex_digit_display_2 (.value({1'b0, ENCRYPTED_I7, ENCRYPTED_I6, ENCRYPTED_I5}));  // open: dp
  not not_18 (FF7, xor_17_out);

  // Other names for the same wires on the sheet: I5 = ANCHOR[0]; I6 = ANCHOR[1]; I7 = ANCHOR[2];
  //   KEY_MEGA[3:0] = {K6, K2, K4, K1}
endmodule

module KeyGenMixer (
  input  in_1,
  input  in_2,
  input  in_3,
  output out_4
);

  wire and_1_out;

  and and_1 (and_1_out, in_1, in_2);
  xor xor_1 (out_4, and_1_out, in_3);
endmodule

module Complex_Encrypter (
  input  [2:0] in_1,
  input  [3:0] in_2,
  output [3:0] out_3
);

  and and_1 (out_3[0], in_1[2], in_1[1], in_2[1], in_2[2], in_1[2]);
  or or_1 (out_3[1], in_1[0], in_2[3], in_1[2], in_2[0], in_1[1]);
  nand nand_1 (out_3[2], in_1[1], in_1[0], in_1[0], in_2[2], in_2[0]);
  nor nor_1 (out_3[3], in_2[0], in_1[1], in_2[3], in_1[2], in_1[1]);

  // Other names for the same wires on the sheet: D1 = in_1[0]; D2 = in_1[1]; D3 = in_1[2]; K1 = in_2[0]; K2 = in_2[1];
  //   K3 = in_2[2]; K4 = in_2[3]
endmodule
