// Logisim project simple_text_cypher.circ as structural Verilog: 1 circuit, main circuit main
module main (
);

  wire button_1_out, CLK, clock_1_out, d_ff_7_q, ENCRYPTED_I1, ENCRYPTED_I2, ENCRYPTED_I3, ENCRYPTED_I4,
       ENCRYPTED_I5, ENCRYPTED_I6, ENCRYPTED_I7, I1, I2, I3, I4, I5, I6, I7, K1, K2, K3, K4, K5, K6, K7,
       KB_BUFFER, not_1_out, not_2_out, not_3_out, not_4_out, not_5_out, not_6_out, not_7_out, not_8_out,
       not_9_out, not_10_out, not_11_out, not_12_out, not_13_out, not_14_out, not_15_out, xor_15_out;
  wire [6:0] xor_8_out;

  not not_1 (not_1_out, CLK);
  Keyboard keyboard_1 (.clk(not_1_out), .avail(KB_BUFFER), .data({I7, I6, I5, I4, I3, I2, I1}));  // open: re, clr
  Clock clock_1 (.out(clock_1_out));
  and and_1 (CLK, clock_1_out, KB_BUFFER);
  Button button_1 (.out(button_1_out));
  D_Flip_Flop d_ff_1 (.clk(CLK), .D(K7), .Q(K1), .preset(button_1_out));  // open: Qn, en, reset
  not not_2 (not_2_out, K4);
  not not_3 (not_3_out, K2);
  not not_4 (not_4_out, K5);
  not not_5 (not_5_out, K1);
  not not_6 (not_6_out, K7);
  not not_7 (not_7_out, K3);
  not not_8 (not_8_out, K6);
  D_Flip_Flop d_ff_2 (.clk(CLK), .D(K1), .Q(K2));  // open: Qn, preset, en, reset
  xor xor_1 (ENCRYPTED_I1, I1, not_2_out);
  xor xor_2 (ENCRYPTED_I2, I2, not_3_out);
  xor xor_3 (ENCRYPTED_I3, I3, not_4_out);
  xor xor_4 (ENCRYPTED_I4, I4, not_5_out);
  xor xor_5 (ENCRYPTED_I5, I5, not_6_out);
  xor xor_6 (ENCRYPTED_I6, I6, not_7_out);
  xor xor_7 (ENCRYPTED_I7, I7, not_8_out);
  D_Flip_Flop d_ff_3 (.clk(CLK), .D(K2), .Q(K3));  // open: Qn, preset, en, reset
  D_Flip_Flop d_ff_4 (.clk(CLK), .D(K3), .Q(K4));  // open: Qn, preset, en, reset
  not not_9 (not_9_out, K4);
  not not_10 (not_10_out, K2);
  not not_11 (not_11_out, K5);
  not not_12 (not_12_out, K1);
  not not_13 (not_13_out, K7);
  not not_14 (not_14_out, K3);
  not not_15 (not_15_out, K6);
  D_Flip_Flop d_ff_5 (.clk(CLK), .D(K4), .Q(K5));  // open: Qn, preset, en, reset
  xor xor_8 (xor_8_out[0], ENCRYPTED_I1, not_9_out);
  xor xor_9 (xor_8_out[1], ENCRYPTED_I2, not_10_out);
  xor xor_10 (xor_8_out[2], ENCRYPTED_I3, not_11_out);
  xor xor_11 (xor_8_out[3], ENCRYPTED_I4, not_12_out);
  xor xor_12 (xor_8_out[4], ENCRYPTED_I5, not_13_out);
  xor xor_13 (xor_8_out[5], ENCRYPTED_I6, not_14_out);
  xor xor_14 (xor_8_out[6], ENCRYPTED_I7, not_15_out);
  D_Flip_Flop d_ff_6 (.clk(CLK), .D(K5), .Q(K6));  // open: Qn, preset, en, reset
  Hex_Digit_Display hex_digit_display_1 (.value({ENCRYPTED_I4, ENCRYPTED_I3, ENCRYPTED_I2, ENCRYPTED_I1}));  // open: dp
  D_Flip_Flop d_ff_7 (.clk(CLK), .D(K6), .Q(d_ff_7_q));  // open: Qn, preset, en, reset
  Hex_Digit_Display hex_digit_display_2 (.value({1'b0, ENCRYPTED_I7, ENCRYPTED_I6, ENCRYPTED_I5}));  // open: dp
  TTY tty_1 (.data(xor_8_out), .clk(CLK));  // open: we, clr
  xor xor_15 (xor_15_out, d_ff_7_q, K6);
  not not_16 (K7, xor_15_out);
endmodule
